// Logisim project Lab One Circuits.circ as structural Verilog: 5 circuits, main circuit 3 IN NAND
module _3_IN_NAND (
  input  A,
  input  B,
  input  C,
  input  A_2,
  input  B_2,
  input  C_2,
  output Output,
  output Output_2
);

  wire nand_1_out, transistor_1_out, transistor_4_out, transistor_5_out, transistor_9_out;

  Transistor transistor_1 (.in(1'b1), .out(transistor_1_out), .gate(A_2));
  Transistor #(.gate("br")) transistor_2 (.in(1'b1), .out(transistor_1_out), .gate(B_2));
  Transistor #(.\type ("n")) transistor_3 (.in(transistor_4_out), .out(transistor_1_out), .gate(A_2));
  Transistor #(.\type ("n"), .gate("br")) transistor_4 (.in(1'b0), .out(transistor_4_out), .gate(B_2));
  nand nand_1 (nand_1_out, A, B);
  Transistor transistor_5 (.in(1'b1), .out(transistor_5_out), .gate(transistor_1_out));
  Transistor #(.\type ("n")) transistor_6 (.in(1'b0), .out(transistor_5_out), .gate(transistor_1_out));
  nand nand_2 (Output, ~nand_1_out, C);  // NAND_Gate
  Transistor transistor_7 (.in(1'b1), .out(Output_2), .gate(transistor_5_out));
  Transistor #(.\type ("n")) transistor_8 (.in(transistor_9_out), .out(Output_2), .gate(transistor_5_out));
  Transistor #(.\type ("n"), .gate("br")) transistor_9 (.in(1'b0), .out(transistor_9_out), .gate(C_2));
  Transistor #(.gate("br")) transistor_10 (.in(1'b1), .out(Output_2), .gate(C_2));
endmodule

module _3_IN_NOR (
  input  A,
  input  B,
  input  C,
  input  A_2,
  input  B_2,
  input  C_2,
  output Output,
  output Output_2
);

  wire nor_1_out, transistor_1_out, transistor_2_out, transistor_5_out, transistor_8_out;

  Transistor transistor_1 (.in(1'b1), .out(transistor_1_out), .gate(A_2));
  Transistor #(.gate("br")) transistor_2 (.in(transistor_1_out), .out(transistor_2_out), .gate(B_2));
  Transistor #(.\type ("n")) transistor_3 (.in(1'b0), .out(transistor_2_out), .gate(A_2));
  Transistor #(.\type ("n"), .gate("br")) transistor_4 (.in(1'b0), .out(transistor_2_out), .gate(B_2));
  nor nor_1 (nor_1_out, A, B);
  Transistor transistor_5 (.in(1'b1), .out(transistor_5_out), .gate(transistor_2_out));
  Transistor #(.\type ("n")) transistor_6 (.in(1'b0), .out(transistor_5_out), .gate(transistor_2_out));
  nor nor_2 (Output, ~nor_1_out, C);  // NOR_Gate
  Transistor #(.\type ("n")) transistor_7 (.in(1'b0), .out(Output_2), .gate(transistor_5_out));
  Transistor transistor_8 (.in(1'b1), .out(transistor_8_out), .gate(transistor_5_out));
  Transistor #(.gate("br")) transistor_9 (.in(transistor_8_out), .out(Output_2), .gate(C_2));
  Transistor #(.\type ("n"), .gate("br")) transistor_10 (.in(1'b0), .out(Output_2), .gate(C_2));
endmodule

module _3_IN_XOR (
  input  A,
  input  B,
  input  C,
  output Output
);

  wire nand_1_out, nand_2_out, nand_3_out, nand_4_out, nand_5_out;

  nand nand_1 (nand_1_out, A, B, C);
  nand nand_2 (nand_2_out, ~A, ~B, C);  // NAND_Gate
  nand nand_3 (nand_3_out, ~A, B, ~C);  // NAND_Gate
  nand nand_4 (nand_4_out, A, ~B, ~C);  // NAND_Gate
  nand nand_5 (nand_5_out, nand_1_out, nand_2_out, nand_3_out);
  nand nand_6 (Output, ~nand_5_out, nand_4_out, 1'b1);  // NAND_Gate
endmodule

module _2_1_MUX (
  input  Control,
  input  A,
  input  B,
  input  Control_2,
  input  A_2,
  input  B_2,
  output Output,
  output Output_2
);

  wire nand_1_out, nand_2_out, nand_3_out, transistor_1_out, transistor_3_out, transistor_5_out,
       transistor_8_out, transistor_9_out, transistor_12_out, transistor_16_out;

  Transistor transistor_1 (.in(1'b1), .out(transistor_1_out), .gate(Control_2));
  Transistor #(.\type ("n")) transistor_2 (.in(transistor_3_out), .out(transistor_1_out), .gate(Control_2));
  Transistor #(.\type ("n")) transistor_3 (.in(1'b0), .out(transistor_3_out), .gate(Control_2));
  Transistor #(.gate("br")) transistor_4 (.in(1'b1), .out(transistor_1_out), .gate(Control_2));
  nand nand_1 (nand_1_out, Control, Control);
  Transistor #(.gate("br")) transistor_5 (.in(1'b1), .out(transistor_5_out), .gate(A_2));
  Transistor transistor_6 (.in(1'b1), .out(transistor_5_out), .gate(transistor_1_out));
  Transistor #(.\type ("n")) transistor_7 (.in(transistor_8_out), .out(transistor_5_out), .gate(transistor_1_out));
  Transistor #(.\type ("n"), .gate("br")) transistor_8 (.in(1'b0), .out(transistor_8_out), .gate(A_2));
  Transistor #(.gate("br")) transistor_9 (.in(1'b1), .out(transistor_9_out), .gate(B_2));
  Transistor transistor_10 (.in(1'b1), .out(transistor_9_out), .gate(Control_2));
  Transistor #(.\type ("n")) transistor_11 (.in(transistor_12_out), .out(transistor_9_out), .gate(Control_2));
  Transistor #(.\type ("n"), .gate("br")) transistor_12 (.in(1'b0), .out(transistor_12_out), .gate(B_2));
  nand nand_2 (nand_2_out, nand_1_out, A);
  nand nand_3 (nand_3_out, Control, B);
  nand nand_4 (Output, nand_2_out, nand_3_out);
  Transistor #(.gate("br")) transistor_13 (.in(1'b1), .out(Output_2), .gate(transistor_5_out));
  Transistor transistor_14 (.in(1'b1), .out(Output_2), .gate(transistor_9_out));
  Transistor #(.\type ("n")) transistor_15 (.in(transistor_16_out), .out(Output_2), .gate(transistor_9_out));
  Transistor #(.\type ("n"), .gate("br")) transistor_16 (.in(1'b0), .out(transistor_16_out), .gate(transistor_5_out));
endmodule

module _3_IN_XOR_MOSFET (
  input  A,
  input  B,
  input  C,
  output Output
);

  wire transistor_1_out, transistor_2_out, transistor_4_out, transistor_5_out, transistor_6_out,
       transistor_8_out, transistor_10_out, transistor_12_out, transistor_14_out, transistor_16_out,
       transistor_19_out, transistor_20_out, transistor_21_out, transistor_25_out, transistor_26_out,
       transistor_29_out, transistor_30_out, transistor_33_out, transistor_34_out, transistor_37_out,
       transistor_38_out, transistor_40_out, transistor_41_out, transistor_43_out, transistor_45_out,
       transistor_48_out, transistor_49_out;

  Transistor transistor_1 (.in(1'b1), .out(transistor_1_out), .gate(A));
  Transistor transistor_2 (.in(1'b1), .out(transistor_2_out), .gate(B));
  Transistor #(.\type ("n")) transistor_3 (.in(transistor_4_out), .out(transistor_2_out), .gate(A));
  Transistor #(.\type ("n")) transistor_4 (.in(transistor_5_out), .out(transistor_4_out), .gate(B));
  Transistor #(.\type ("n")) transistor_5 (.in(1'b0), .out(transistor_5_out), .gate(C));
  Transistor transistor_6 (.in(1'b1), .out(transistor_6_out), .gate(A));
  Transistor #(.\type ("n")) transistor_7 (.in(1'b0), .out(transistor_6_out), .gate(A));
  Transistor transistor_8 (.in(1'b1), .out(transistor_8_out), .gate(B));
  Transistor #(.\type ("n")) transistor_9 (.in(1'b0), .out(transistor_8_out), .gate(B));
  Transistor transistor_10 (.in(1'b1), .out(transistor_10_out), .gate(A));
  Transistor #(.\type ("n")) transistor_11 (.in(1'b0), .out(transistor_10_out), .gate(A));
  Transistor transistor_12 (.in(1'b1), .out(transistor_12_out), .gate(C));
  Transistor #(.\type ("n")) transistor_13 (.in(1'b0), .out(transistor_12_out), .gate(C));
  Transistor transistor_14 (.in(1'b1), .out(transistor_14_out), .gate(B));
  Transistor #(.\type ("n")) transistor_15 (.in(1'b0), .out(transistor_14_out), .gate(B));
  Transistor transistor_16 (.in(1'b1), .out(transistor_16_out), .gate(C));
  Transistor #(.\type ("n")) transistor_17 (.in(1'b0), .out(transistor_16_out), .gate(C));
  Transistor transistor_18 (.in(1'b1), .out(transistor_1_out), .gate(C));
  Transistor transistor_19 (.in(1'b1), .out(transistor_19_out), .gate(transistor_6_out));
  Transistor transistor_20 (.in(1'b1), .out(transistor_20_out), .gate(transistor_10_out));
  Transistor transistor_21 (.in(1'b1), .out(transistor_21_out), .gate(A));
  Transistor transistor_22 (.in(1'b1), .out(transistor_19_out), .gate(transistor_8_out));
  Transistor transistor_23 (.in(1'b1), .out(transistor_19_out), .gate(C));
  Transistor #(.\type ("n")) transistor_24 (.in(transistor_25_out), .out(transistor_19_out), .gate(transistor_6_out));
  Transistor #(.\type ("n")) transistor_25 (.in(transistor_26_out), .out(transistor_25_out), .gate(transistor_8_out));
  Transistor #(.\type ("n")) transistor_26 (.in(1'b0), .out(transistor_26_out), .gate(C));
  Transistor transistor_27 (.in(1'b1), .out(transistor_20_out), .gate(B));
  Transistor #(.\type ("n")) transistor_28 (.in(transistor_29_out), .out(transistor_20_out), .gate(transistor_10_out));
  Transistor #(.\type ("n")) transistor_29 (.in(transistor_30_out), .out(transistor_29_out), .gate(B));
  Transistor #(.\type ("n")) transistor_30 (.in(1'b0), .out(transistor_30_out), .gate(transistor_12_out));
  Transistor transistor_31 (.in(1'b1), .out(transistor_21_out), .gate(transistor_14_out));
  Transistor #(.\type ("n")) transistor_32 (.in(transistor_33_out), .out(transistor_21_out), .gate(A));
  Transistor #(.\type ("n")) transistor_33 (.in(transistor_34_out), .out(transistor_33_out), .gate(transistor_14_out));
  Transistor #(.\type ("n")) transistor_34 (.in(1'b0), .out(transistor_34_out), .gate(transistor_16_out));
  Transistor transistor_35 (.in(1'b1), .out(transistor_20_out), .gate(transistor_12_out));
  Transistor transistor_36 (.in(1'b1), .out(transistor_21_out), .gate(transistor_16_out));
  Transistor transistor_37 (.in(1'b1), .out(transistor_37_out), .gate(transistor_2_out));
  Transistor transistor_38 (.in(1'b1), .out(transistor_38_out), .gate(transistor_19_out));
  Transistor #(.\type ("n")) transistor_39 (.in(transistor_40_out), .out(transistor_38_out), .gate(transistor_2_out));
  Transistor #(.\type ("n")) transistor_40 (.in(transistor_41_out), .out(transistor_40_out), .gate(transistor_19_out));
  Transistor #(.\type ("n")) transistor_41 (.in(1'b0), .out(transistor_41_out), .gate(transistor_20_out));
  Transistor transistor_42 (.in(1'b1), .out(transistor_37_out), .gate(transistor_20_out));
  Transistor transistor_43 (.in(1'b1), .out(transistor_43_out), .gate(transistor_38_out));
  Transistor #(.\type ("n")) transistor_44 (.in(1'b0), .out(transistor_43_out), .gate(transistor_38_out));
  Transistor transistor_45 (.in(1'b1), .out(transistor_45_out), .gate(transistor_43_out));
  Transistor transistor_46 (.in(1'b1), .out(Output), .gate(transistor_21_out));
  Transistor #(.\type ("n")) transistor_47 (.in(transistor_48_out), .out(Output), .gate(transistor_43_out));
  Transistor #(.\type ("n")) transistor_48 (.in(transistor_49_out), .out(transistor_48_out), .gate(transistor_21_out));
  Transistor #(.\type ("n"), .gate("br")) transistor_49 (.in(1'b0), .out(transistor_49_out), .gate(1'b1));
  Transistor #(.gate("br")) transistor_50 (.in(1'b1), .out(transistor_45_out), .gate(1'b1));
endmodule
